// Logisim project ex4.circ as structural Verilog: 5 circuits, main circuit RotRight
module RotRight (
  input  [15:0] INPUT0,
  input  [3:0] AMOUNT,
  output [15:0] OUTPUT0
);

  wire [15:0] multiplexer_1_out, multiplexer_2_out, multiplexer_3_out, r1, r2, r4, r8;

  Multiplexer #(.width(16)) multiplexer_1 (.in0(INPUT0), .in1(r1), .out(multiplexer_1_out), .sel(AMOUNT[0]));
  rot1 rot1_1 (.in_1(INPUT0), .out_2(r1));
  rot2 rot2_1 (.in_1(multiplexer_1_out), .out_2(r2));
  Multiplexer #(.width(16)) multiplexer_2 (.in0(multiplexer_1_out), .in1(r2), .out(multiplexer_2_out), .sel(AMOUNT[1]));
  Multiplexer #(.width(16)) multiplexer_3 (.in0(multiplexer_2_out), .in1(r4), .out(multiplexer_3_out), .sel(AMOUNT[2]));
  rot4 rot4_1 (.in_1(multiplexer_2_out), .out_2(r4));
  Multiplexer #(.width(16)) multiplexer_4 (.in0(multiplexer_3_out), .in1(r8), .out(OUTPUT0), .sel(AMOUNT[3]));
  rot8 rot8_1 (.in_1(multiplexer_3_out), .out_2(r8));

  // Other names for the same wires on the sheet: a0 = AMOUNT[0]; a1 = AMOUNT[1]; a2 = AMOUNT[2]; a3 = AMOUNT[3]
endmodule

module rot1 (
  input  [15:0] in_1,
  output [15:0] out_2
);


  assign out_2 = {in_1[0], in_1[15:1]};

  // Other names for the same wires on the sheet: t1[14:0] = in_1[15:1]; t0 = in_1[0]
endmodule

module rot2 (
  input  [15:0] in_1,
  output [15:0] out_2
);


  assign out_2 = {in_1[1:0], in_1[15:2]};

  // Other names for the same wires on the sheet: t1[13:0] = in_1[15:2]; t0[1:0] = in_1[1:0]
endmodule

module rot4 (
  input  [15:0] in_1,
  output [15:0] out_2
);


  assign out_2 = {in_1[3:0], in_1[15:4]};

  // Other names for the same wires on the sheet: t1[11:0] = in_1[15:4]; t0[3:0] = in_1[3:0]
endmodule

module rot8 (
  input  [15:0] in_1,
  output [15:0] out_2
);


  assign out_2 = {in_1[7:0], in_1[15:8]};

  // Other names for the same wires on the sheet: t1[7:0] = in_1[15:8]; t0[7:0] = in_1[7:0]
endmodule
